# Fritzing sketch Wiring (saved by Fritzing 0.9.3b)
breadboards: 1

parts:
  Part1 = Arduino Mega ADK (Rev3)
  J1 = Basic Servo
  J2 = Basic Servo
  J3 = Basic Servo
  J4 = Basic Servo
  J5 = Basic Servo
  Part2 = 16-Channel 12-bit PWM Servo Driver - I2C [part_number=815]

nets:
  N1: Part1.D21/SCL, Part2.SCL
  N2: Part1.D20/SDA, Part2.SDA
  GND: J1.gnd, J2.gnd, J3.gnd, J4.gnd, J5.gnd, Part2.GND
  VCC: J1.vcc, J2.vcc, J3.vcc, J4.vcc, J5.vcc, Part2.5.0V
  N3: J1.pulse, Part2.PWM15
  N4: J2.pulse, Part2.PWM13
  N5: J3.pulse, Part2.PWM14
  N6: J4.pulse, Part2.PWM11
  N7: J5.pulse, Part2.PWM12

custom parts:
  16-Channel 12-bit PWM Servo Driver - I2C: You want to make a cool robot, maybe a hexapod walker, or maybe just a piece of art with a lot of moving parts. Or maybe you want to drive a lot of LEDs with precise PWM output. Using only two pins, control 16 free-running PWM outputs! You can even chain up 62 breakouts to control up to 992 PWM outputs.
